# Fritzing sketch Pilarm (saved by Fritzing 0.9.2b)
breadboards: 1

parts:
  J1 = Cobbler Plus Cable
  Raspberry_Pi1 = Raspberry Pi B+
  SW1 = PowerSwitch Tail II
  PIR1 = PIR sensor
  KEYPAD1 = Membrane Matrix Keypad
  AMP1 = MAX98306_Stereo_Amplifier
  U1 = AUDIO-JACK2 [package=audio-jack-3.5mm-smd]
  BATT1 = 4xAA Switchable Battery Pack w/Bare Wire
  SP1 = SPEAKER [package=pcb_mount_speaker]
  LED1 = LEDs [package=led10mm]
  LED2 = LEDs [package=led10mm]
  R1 = Resistor [tolerance=±5% resistance=220 package="0805 [SMD]"]
  R2 = Resistor [tolerance=±5% resistance=220 package="0805 [SMD]"]

nets:
  3V3: J1.3V3, PIR1.VDD
  N1: J1.GND#5, LED1.C, LED2.C
  N2: J1.#4, KEYPAD1.5
  N3: J1.#17, KEYPAD1.6
  N4: J1.#18, KEYPAD1.1
  N5: J1.#27, KEYPAD1.7
  N6: J1.#22, PIR1.SIG
  N7: J1.#23, KEYPAD1.2
  N8: J1.#24, KEYPAD1.3
  N9: J1.#25, KEYPAD1.4
  N10: J1.#6, SW1.+in
  N11: J1.#16, R1.Pin_0
  N12: J1.GND#38, SW1.-in, PIR1.GND
  N13: J1.#21, R2.Pin_0
  3V3_2: J1.3.3V#41, J1.3.3V#57, Raspberry_Pi1.3v3, Raspberry_Pi1.3V3
  5V: J1.5V, Raspberry_Pi1.5V
  N14: J1.GPIO_2, Raspberry_Pi1.GPIO2
  N15: J1.GPIO_3, Raspberry_Pi1.GPIO3
  N16: J1.GND#46, J1.GND#49, J1.GND#54, J1.GND#60, J1.GND#65, J1.GND#70, J1.GND#74, J1.GND#79, Raspberry_Pi1.GND
  N17: J1.GPIO_4, Raspberry_Pi1.GIPO4
  N18: J1.GPIO_14, Raspberry_Pi1.GIPO14
  N19: J1.GPIO_15, Raspberry_Pi1.GIPO15
  N20: J1.GPIO_17, Raspberry_Pi1.GIPO17
  N21: J1.GPIO_18, Raspberry_Pi1.GIPO18
  N22: J1.GPIO_27, Raspberry_Pi1.GIPO27
  N23: J1.GPIO_22, Raspberry_Pi1.GIPO22
  N24: J1.GPIO_23, Raspberry_Pi1.GIPO23
  N25: J1.GPIO_24, Raspberry_Pi1.GIPO24
  N26: J1.GPIO_10, Raspberry_Pi1.GIPO10
  N27: J1.GPIO_9, Raspberry_Pi1.GIPO9
  N28: J1.GPIO_25, Raspberry_Pi1.GIPO25
  N29: J1.GPIO_11, Raspberry_Pi1.GIPO11
  N30: J1.GPIO_8, Raspberry_Pi1.GIPO8
  N31: J1.GPIO_7, Raspberry_Pi1.GIPO7
  N32: J1.ID_SD, Raspberry_Pi1.ID_SD
  N33: J1.ID_SC, Raspberry_Pi1.ID_SC
  N34: J1.GPIO_5, Raspberry_Pi1.GIPO5
  N35: J1.GPIO_6, Raspberry_Pi1.GIPO6
  N36: J1.GPIO_12, Raspberry_Pi1.GIPO12
  N37: J1.GPIO_13, Raspberry_Pi1.GIPO13
  N38: J1.GPIO_19, Raspberry_Pi1.GIPO19
  N39: J1.GPIO_16, Raspberry_Pi1.GIPO16
  N40: J1.GPIO_26, Raspberry_Pi1.GIPO26
  N41: J1.GPIO_20, Raspberry_Pi1.GIPO20
  N42: J1.GPIO_21, Raspberry_Pi1.GIPO21
  N43: AMP1.connector1, BATT1.POS
  N44: AMP1.connector2, BATT1.NEG
  N45: AMP1.connector4, U1.RSH
  N46: AMP1.connector6, U1.TIP
  N47: AMP1.connector7, U1.TSH
  N48: AMP1.connector12, SP1.+
  N49: AMP1.connector13, SP1.-
  N50: LED1.A, R1.Pin_1
  N51: LED2.A, R2.Pin_1

notes:
  PowerSwitch gets plugged into the flashing light.
  You don't need a breakout board for the cable here, you can just cut an 1/8" audio cable and wire it directly to the audio amp. This breakout here is just for illustration.

custom parts:
  Cobbler Plus Cable: The Cobbler Plus is an add on prototyping board from Adafruit specifically designed for the Raspberry Pi B+ that can break out all those tasty power, GPIO, I2C and SPI pins from the 40-pin header onto a solderless breadboard. This set will make "cobbling together" prototypes with the Pi super easy. The Cobbler Plus can plug into any solderless breadboard.
  Raspberry Pi B+: The awesome Raspberry Pi ARM Board with 40 pin gipo. Ready for special designed Raspberry Pi B+ Hat (Hardware attached (on) top)
  Membrane Matrix Keypad: Membrane Matrix 3x4 Keypad
  4xAA Switchable Battery Pack w/Bare Wire: 4xAA Switchable Battery Pack with Bare Wire connection
